# Fritzing sketch ardukey-arduino-leonardo (saved by Fritzing 0.9.2b)

parts:
  Bauteil1 = Arduino Leonardo (Rev3b)
  S1 = Pushbutton [package="[THT]"]

nets:
  N1: Bauteil1.GND, S1.Pin_4
  N2: Bauteil1.D12/A11, S1.Pin_2
